# Fritzing sketch SensorHW (saved by Fritzing 0.8.3b)
breadboards: 1

parts:
  MLX90620_Infrared_Thermometer = MLX90614 Infrared Thermometer
  C1 = Ceramic Capacitor [capacitance=0.1µF package="100 mil [THT, multilayer]"]
  D1 = Rectifier Diode [part_number=1N4001 package="300 mil [THT]"]
  R1 = Resistor [tolerance=±5% resistance=4.7k package=THT]
  R2 = Resistor [tolerance=±5% resistance=4.7k package=THT]
  Arduino_Uno_R3 = Arduino Uno (Rev3)
  JY-MCU_Bluetooth = JY-MCU

nets:
  N1: MLX90620_Infrared_Thermometer.PWM_/_SDA, R1.Pin_0, Arduino_Uno_R3.A4/SDA
  N2: MLX90620_Infrared_Thermometer.VDD, C1.1, D1.cathode
  GND: MLX90620_Infrared_Thermometer.VSS, C1.0, Arduino_Uno_R3.GND, JY-MCU_Bluetooth.GND
  N3: MLX90620_Infrared_Thermometer.SCL_/_Vz, R2.Pin_0, Arduino_Uno_R3.A5/SCL
  3V3: D1.anode, R1.Pin_1, R2.Pin_1, Arduino_Uno_R3.3V3, JY-MCU_Bluetooth.VCC
  N4: Arduino_Uno_R3.D0/RX, JY-MCU_Bluetooth.RX
  N5: Arduino_Uno_R3.D1/TX, JY-MCU_Bluetooth.TX

notes:
  MLX90620
  JY-MCU

custom parts:
  MLX90614 Infrared Thermometer: The MLX90614 is an Infra Red thermometer for non contact temperature measurements. Both the IR sensitive thermopile detector chip and the signal conditioning ASSP are integrated in the same TO-39 can.
  JY-MCU: Description: The Bluetooth Mate is very similar to our BlueSMiRF modem, but it is designed specifically to be used with our Arduino Pros and LilyPad Arduinos. These modems work as a serial (RX/TX) pipe, and are a great wireless replacement for serial cables. Any serial stream from 9600 to 115200bps can be passed seamlessly from your computer to your target. Bluetooth Mate has the same pin out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
